# Fritzing sketch Door Remote (saved by Fritzing 0.9.3b)
circuit board: 8.46667cm x 5.64444cm
breadboards: 1

parts:
  M1 = RioRand LM2596
  LED1 = LED - 5mm [color="Red (633nm)" package="5 mm [THT]"]
  LED2 = LED - 5mm [color="Green (570nm)" package="5 mm [THT]"]
  DS1 = DS18B20 1-Wire Temperature Sensor [part_number=DS18B20]
  R1 = Resistor [tolerance=±5% resistance=100 package="0402 [SMD]"]
  R3 = Resistor [tolerance=±5% resistance=150 package="0402 [SMD]"]
  R4 = Resistor [tolerance=±5% resistance=4.7k package="0402 [SMD]"]
  U1 = NodeMCU V3.0
  S1 = Reed switch [package=THT]
  S2 = Reed switch [package=THT]
  KY-1 = Keyes Relay [package=THT]
  S3 = Momentary Switch [package=ksa_sealed_tac_switch]

nets:
  N1: M1.Pin_3, KY-1.power
  N2: M1.Pin_4, LED1.cathode, LED2.cathode, DS1.GND, S1.pin_1, S2.pin_1, KY-1.ground, S3.2, S3.4
  N3: LED1.anode, R3.Pin_0
  N4: LED2.anode, R1.Pin_0
  N5: DS1.DQ, R4.Pin_1
  VDD: DS1.VDD, R4.Pin_0, U1.3V3
  N6: U1.D0, S3.1, S3.3
  N7: U1.D5, S2.pin_2
  N8: U1.D6, S1.pin_2

custom parts:
  NodeMCU V3.0: ESP8266 based NodeMCU
  Keyes Relay: The Keyes 5V relay module is suitable for SCM development, home appliance control. It uses a 5V~12V TIL control signal which can control DC / AC signal.
